# Fritzing sketch babybox (saved by Fritzing 0.9.2b)
breadboards: 1

parts:
  LDR = Photocell (LDR) [package=THT]
  Buzzer = Piezo Speaker
  DHT11 = Humidity and Temperature Sensor RHT03
  R2 = Resistor [tolerance=±5% resistance=10k package="1206 [SMD]"]
  R3 = Resistor [tolerance=±5% resistance=100 package="1206 [SMD]"]
  U4 = MAX1555 Lithium Charger IC [package=sot23-5]
  Power_plug_5V = Power plug
  Pro_mini = Arduino Mini (Rev5)
  U2 = LMZ14203 [package=to-pmod-7]
  NRF24 = 2.4GHz Low Power Transceiver [package=qfn20]
  Battery = Battery block 9V
  ky-037 = Breakout Board for Electret Microphone

nets:
  N1: LDR.pin_0, R2.Pin_1, Pro_mini.A6
  GND: LDR.pin_1, Buzzer.pin1, DHT11.GND_2, Power_plug_5V.GND, Pro_mini.GND, U2.GND, ky-037.GND
  N2: Buzzer.pin2, R3.Pin_1
  VCC: DHT11.Vcc, R2.Pin_0, Pro_mini.5V, ky-037.VCC
  N3: DHT11.Data-signal, Pro_mini.A3
  N4: R3.Pin_0, Pro_mini.D5_PWM
  N5: U4.DC, Battery.+
  N6: U4.BATT, Battery.-
  VCC_2: Power_plug_5V.VCC, Pro_mini.VCC
  N7: Pro_mini.A0, ky-037.AUD
  N8: U2.FB, NRF24.VDD
  N9: U2.VOUT, NRF24.VSS
