# Fritzing sketch arduino_nrf_dht11_ldr_battery (saved by Fritzing 0.9.2b)
perfboards: 1

parts:
  Componente1 = Arduino Pro Mini v13
  R1 = Photocell (LDR) [package=THT]
  S1 = Toggle Switch [package=THT]
  C2 = Electrolytic Capacitor [capacitance=1µF package="100 mil [THT, electrolytic]"]
  R2 = Resistor [tolerance=±5% resistance=1M package=THT]
  RHT1 = Humidity and Temperature Sensor RHT03
  Power_plug1 = Power plug
  MIRF2 = MIRF [package=mirf]
  VCC1 = Battery block 9V
  R3 = Resistor [tolerance=±5% resistance=470k package=THT]

nets:
  VCC: Componente1.VCC, R1.pin_0, C2.+, RHT1.Vcc, MIRF2.1
  N1: Componente1.GND, C2.-, RHT1.GND_2, MIRF2.7, R3.Pin_1
  N2: Componente1.A1, R1.pin_1
  N3: Componente1.D3_PWM, RHT1.Data-signal
  N4: S1.L1, Power_plug1.VCC, VCC1.+
  N5: S1.COM, R2.Pin_0
  N6: R2.Pin_1, R3.Pin_0
  N7: Power_plug1.GND, VCC1.-
